# Fritzing sketch _1_WasherNotifier_Webhook (saved by Fritzing 0.9.3b)
breadboards: 1

parts:
  U1 = NodeMCU V1.0
  LED1 = LED - 5mm [color="Red (633nm)" package="5 mm [THT]"]
  LED2 = LED - 5mm [color="Green (555nm)" package="5 mm [THT]"]
  R3 = Resistor [tolerance=±5% resistance=330 package=THT]
  R4 = Resistor [tolerance=±5% resistance=330 package=THT]
  R2 = Resistor [tolerance=±1% resistance=1k package=THT]
  R5 = Photocell (LDR) [package=THT]

nets:
  N1: U1.D0, R4.Pin_0
  N2: U1.D1, R3.Pin_0
  N3: U1.3V3, R5.pin_1
  N4: U1.GND, LED1.cathode, LED2.cathode, R2.Pin_1
  N5: U1.A0, R2.Pin_0, R5.pin_0
  N6: LED1.anode, R3.Pin_1
  N7: LED2.anode, R4.Pin_1

custom parts:
  NodeMCU V1.0: ESP8266 based NodeMCU
